# Fritzing sketch Roomba_Wiring (saved by Fritzing 0.9.9b)

parts:
  U3 = DIN7 [package=din7]  # not connected
  U4 = ISL29102 [package=odfn6]
  U5 = Buck Converter [package=odfn6]
  WeMos_D1_Mini1 = WeMos D1 Mini
  Q1 = PNP-Transistor [part_number=2N3906 package="TO92 [THT]"]

nets:
  N1: U4.NC, U5.Roomba_+
  N2: U4.REXT, WeMos_D1_Mini1.3V3
  N3: U4.VOUT, WeMos_D1_Mini1.G
  N4: WeMos_D1_Mini1.RX, Q1.E

notes:
  PNP
  Transistor
  2N3906
  D1 mini
  Roomba
  OI Port
  Buck Converter
  14V -> 3,3V
